# Fritzing sketch picoArduino (saved by Fritzing 0.9.3b)
breadboards: 1

parts:
  Mod1 = Raspberry Pi Pico
  LED1 = LED - 5mm [color="Red (633nm)" package="5 mm [THT]"]
  LED2 = LED - 5mm [color="Green (565nm)" package="5 mm [THT]"]
  LED3 = LED - 5mm [color="Orange (620nm)" package="5 mm [THT]"]
  R1 = Resistor [tolerance=±5% resistance=470 package="1206 [SMD]"]
  R2 = Resistor [tolerance=±5% resistance=470 package="1206 [SMD]"]
  R3 = Resistor [tolerance=±5% resistance=470 package="1206 [SMD]"]
  U1 = POT [package=pot_mammoth]

nets:
  N1: Mod1.pin_3, Mod1.pin_8, Mod1.pin_13, Mod1.pin_18, Mod1.pin_23, Mod1.pin_28, Mod1.pin_33, Mod1.pin_38, Mod1.pin_42, LED1.cathode, LED2.cathode, LED3.cathode, U1.E
  N2: Mod1.pin_24, R3.Pin_1
  N3: Mod1.pin_25, R2.Pin_1
  N4: Mod1.pin_26, R1.Pin_1
  N5: Mod1.pin_36, U1.S
  N6: LED1.anode, R3.Pin_0
  N7: LED2.anode, R2.Pin_0
  N8: LED3.anode, R1.Pin_0

custom parts:
  Raspberry Pi Pico: Raspberry Pi Pico. Based around the RP2040 microcontroller the Pico is a low cost microcontroller device bringing Raspberry Pi quality, cost, and easy of use to the microcontroller space. Jan 2021, Split part in to two versions: tht (this one) and SMD. This one will drill holes for a .1 in header in pcb to allow plugging in the module as well as providing pads to solder the module to the top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
